# Fritzing sketch Overall Project scheme (saved by Fritzing 0.9.3b)
breadboards: 1

parts:
  Салқындатқыш = DC Motor
  Ылғалдатқыш = DC Motor
  U1 = NodeMCU V1.0
  Жылытқыш = DC Motor
  DHT1 = DHT11 Humitidy and Temperature Sensor

nets:
  N1: Салқындатқыш.pin_1, U1.D6
  GND: Салқындатқыш.pin_2, Ылғалдатқыш.pin_2, U1.GND, Жылытқыш.pin_2, DHT1.GND
  N2: Ылғалдатқыш.pin_1, U1.D7
  N3: U1.D4, DHT1.DATA
  N4: U1.D5, Жылытқыш.pin_1
  3V3: U1.3V3, DHT1.VDD

notes:
  Салқындатқыш
  Жылытқыш
  Ылғалдатқыш
  DHT11 сенсоры
  NodeMCU ESP8266 микроконтроллері

custom parts:
  NodeMCU V1.0: ESP8266 based NodeMCU
  DHT11 Humitidy and Temperature Sensor: DHT11 Humidity and Temperature Sensor
